// Logisim project final_project.circ as structural Verilog: 36 circuits, main circuit main
module main (
);

  wire c_flag, clk, compare_8bit_1_same, Disp_Write_EN, Flag_Write_EN, Is_Jump, jump_en_logic_1_load_enable,
       reset, Write_EN;
  wire [1:0] Reg_Source_Sel;
  wire [3:0] Addr_A, Addr_B, Addr_D, ALU_Sel;
  wire [6:0] multiplexer_2_out;
  wire [7:0] alu_8bit_1_alu_out, counter_1_q, multiplexer_1_out, multiplexer_3_out, Port_A, Port_B;
  wire [11:0] Opcode;

  Jump_EN_Logic jump_en_logic_1 (
    .is_jump(Is_Jump), .jump_type(Addr_D[1:0]), .c(c_flag), .load_enable(jump_en_logic_1_load_enable));
  ROM #(.addrWidth(12), .dataWidth(10)) InstructionDecoder (
    .addr(Opcode), .data({Flag_Write_EN, Is_Jump, ALU_Sel, Reg_Source_Sel, Disp_Write_EN, Write_EN}));
  Multiplexer #(.select(2), .width(8)) multiplexer_1 (
    .in0(Port_A), .in1({Addr_A, Addr_B}), .in2({Addr_A, Addr_B}), .in3({Addr_A, Addr_B}),
    .out(multiplexer_1_out), .sel(Addr_D[1:0]));
  Counter counter_1 (
    .clr(reset), .load(jump_en_logic_1_load_enable), .up(1'b1), .count(1'b1), .clk(clk),
    .D(multiplexer_1_out), .Q(counter_1_q));  // open: carry
  ROM #(.dataWidth(24)) ProgramPROM (.addr(counter_1_q), .data({Opcode, Addr_D, Addr_A, Addr_B}));
  Clock global_clk (.out(clk));
  Multiplexer #(.width(7)) multiplexer_2 (
    .in0(Port_A[6:0]), .in1({Addr_A[2:0], Addr_B}), .out(multiplexer_2_out), .sel(Addr_D[0]));
  // Probe on multiplexer_2_out
  TTY tty_1 (.data(multiplexer_2_out), .clk(clk), .we(Disp_Write_EN), .clr(reset));
  Button u_Reset (.out(reset));
  Multiplexer #(.select(2), .width(8)) multiplexer_3 (
    .in0({Addr_A, Addr_B}), .in1(alu_8bit_1_alu_out), .in2(Port_A), .out(multiplexer_3_out),
    .sel(Reg_Source_Sel));  // open: in3
  // Probe on multiplexer_3_out
  Compare_8bit compare_8bit_1 (.A(Port_A), .B(Port_B), .Same(compare_8bit_1_same));
  Reg_file_3port reg_file_3port_1 (
    .WE(Write_EN), .RAddr_A(Addr_A), .WAddr(Addr_D), .RAddr_B(Addr_B), .Data_in(multiplexer_3_out),
    .reset(reset), .Clk(clk), .Port_A(Port_A), .Port_B(Port_B));
  Register_1bit register_1bit_1 (
    .Din(compare_8bit_1_same), .Write_EN(Flag_Write_EN), .reset(reset), .clk(clk), .Dout(c_flag));
  ALU_8bit alu_8bit_1 (.A(Port_A), .B(Port_B), .Func(ALU_Sel), .ALU_OUT(alu_8bit_1_alu_out));
  // Probe on alu_8bit_1_alu_out

  // Other names for the same wires on the sheet: Data[7:0] = {Addr_A, Addr_B}; Display_data_sel = Addr_D[0];
  //   LD_Sel[1:0] = Addr_D[1:0]

  // Notes on the sheet:
  //   contents of InstructionDecoder (hex, n*v repeats v):
  //   0 1 9 2 5 15 25 35 45 55 65 100 85 95 200 75 2
  //   contents of ProgramPROM (hex, n*v repeats v):
  //   3153 3174 3161 3172 3174 310a 1f30 1e00 1103 1204 3148 3169 312c 3120 3142 314a 3121 310a 3133 312b
  //   3134 313d 7312 703f 3000 310a 3133 312a 3133 313d 7311 7331 703f 3000 310a 3128 3173 3129 3120 3134
  //   312d 3133 313d a410 c440 7324 703f 3000 310a 3128 3168 3129 3120 3134 312d 3133 313d f321 703f 3000
  //   310a 316c 313a cee0 70ef 3000 310a e0e1 b30a 1e00 310a 3133 3120 3158 314f 3152 3120 3134 313d 4312
  //   703f 3000 310a 3133 3126 3134 313d 5312 703f 3000 310a 3133 317c 3134 313d 6312 703f 3000 310a 316c
  //   313a cee0 70ef 3000 310a e0e1 b346 1e00 310a 3133 313e 313e 3131 313d 8310 703f 3000 310a 3134 313c
  //   313c 3131 313d 9320 703f 3000 310a 316c 313a cee0 70ef 3000 310a e0e1 b36c 1e00 310a 3133 312d 3131
  //   313d 2410 d440 704f 3000 310a 3144 316f 316e 3165 310a 310a 1e00 b10a
endmodule

module Register_1bit (
  input  Din,
  input  Write_EN,
  input  reset,
  input  clk,
  output Dout
);

  wire multiplexer_1_out;

  D_Flip_Flop d_ff_1 (.D(multiplexer_1_out), .clk(clk), .Q(Dout), .reset(reset));  // open: Qn, preset
  Multiplexer multiplexer_1 (.in0(Dout), .in1(Din), .out(multiplexer_1_out), .sel(Write_EN));
endmodule

module Register_4bit (
  input  [3:0] Din,
  input  Write_EN,
  input  reset,
  input  clk,
  output [3:0] Dout
);

  Register_1bit register_1bit_1 (.Din(Din[0]), .Write_EN(Write_EN), .reset(reset), .clk(clk), .Dout(Dout[0]));
  Register_1bit register_1bit_2 (.Din(Din[1]), .Write_EN(Write_EN), .reset(reset), .clk(clk), .Dout(Dout[1]));
  Register_1bit register_1bit_3 (.Din(Din[2]), .Write_EN(Write_EN), .reset(reset), .clk(clk), .Dout(Dout[2]));
  Register_1bit register_1bit_4 (.Din(Din[3]), .Write_EN(Write_EN), .reset(reset), .clk(clk), .Dout(Dout[3]));
endmodule

module Register_8bit (
  input  [7:0] Din,
  input  Write_EN,
  input  reset,
  input  clk,
  output [7:0] Dout
);

  Register_4bit register_4bit_1 (.Din(Din[3:0]), .Write_EN(Write_EN), .reset(reset), .clk(clk), .Dout(Dout[3:0]));
  Register_4bit register_4bit_2 (.Din(Din[7:4]), .Write_EN(Write_EN), .reset(reset), .clk(clk), .Dout(Dout[7:4]));
endmodule

module Reg_file_3port (
  input  WE,
  input  [3:0] RAddr_A,
  input  [3:0] WAddr,
  input  [3:0] RAddr_B,
  input  [7:0] Data_in,
  input  reset,
  input  Clk,
  output [7:0] Port_A,
  output [7:0] Port_B
);

  wire decoder_1_out0, decoder_1_out1, decoder_1_out2, decoder_1_out3, decoder_1_out4, decoder_1_out5,
       decoder_1_out6, decoder_1_out7, decoder_1_out8, decoder_1_out9, decoder_1_out10, decoder_1_out11,
       decoder_1_out12, decoder_1_out13, decoder_1_out14, decoder_1_out15;
  wire [7:0] r0, r1, r2, r3, r4, r5, r6, r7, r8, r9, ra, rb, rc, rd, re, rf;

  Decoder #(.select(4)) decoder_1 (
    .out0(decoder_1_out0), .out1(decoder_1_out1), .out2(decoder_1_out2), .out3(decoder_1_out3),
    .out4(decoder_1_out4), .out5(decoder_1_out5), .out6(decoder_1_out6), .out7(decoder_1_out7),
    .out8(decoder_1_out8), .out9(decoder_1_out9), .out10(decoder_1_out10), .out11(decoder_1_out11),
    .out12(decoder_1_out12), .out13(decoder_1_out13), .out14(decoder_1_out14), .out15(decoder_1_out15),
    .sel(WAddr), .en(WE));
  Register_8bit register_8bit_1 (.Din(Data_in), .Write_EN(decoder_1_out0), .reset(reset), .clk(Clk), .Dout(r0));
  Register_8bit register_8bit_2 (.Din(Data_in), .Write_EN(decoder_1_out1), .reset(reset), .clk(Clk), .Dout(r1));
  Register_8bit register_8bit_3 (.Din(Data_in), .Write_EN(decoder_1_out2), .reset(reset), .clk(Clk), .Dout(r2));
  Register_8bit register_8bit_4 (.Din(Data_in), .Write_EN(decoder_1_out3), .reset(reset), .clk(Clk), .Dout(r3));
  Register_8bit register_8bit_5 (.Din(Data_in), .Write_EN(decoder_1_out4), .reset(reset), .clk(Clk), .Dout(r4));
  Register_8bit register_8bit_6 (.Din(Data_in), .Write_EN(decoder_1_out5), .reset(reset), .clk(Clk), .Dout(r5));
  Register_8bit register_8bit_7 (.Din(Data_in), .Write_EN(decoder_1_out6), .reset(reset), .clk(Clk), .Dout(r6));
  Register_8bit register_8bit_8 (.Din(Data_in), .Write_EN(decoder_1_out7), .reset(reset), .clk(Clk), .Dout(r7));
  Register_8bit register_8bit_9 (.Din(Data_in), .Write_EN(decoder_1_out8), .reset(reset), .clk(Clk), .Dout(r8));
  Register_8bit register_8bit_10 (.Din(Data_in), .Write_EN(decoder_1_out9), .reset(reset), .clk(Clk), .Dout(r9));
  Register_8bit register_8bit_11 (.Din(Data_in), .Write_EN(decoder_1_out10), .reset(reset), .clk(Clk), .Dout(ra));
  Register_8bit register_8bit_12 (.Din(Data_in), .Write_EN(decoder_1_out11), .reset(reset), .clk(Clk), .Dout(rb));
  Register_8bit register_8bit_13 (.Din(Data_in), .Write_EN(decoder_1_out12), .reset(reset), .clk(Clk), .Dout(rc));
  Register_8bit register_8bit_14 (.Din(Data_in), .Write_EN(decoder_1_out13), .reset(reset), .clk(Clk), .Dout(rd));
  Register_8bit register_8bit_15 (.Din(Data_in), .Write_EN(decoder_1_out14), .reset(reset), .clk(Clk), .Dout(re));
  Register_8bit register_8bit_16 (.Din(Data_in), .Write_EN(decoder_1_out15), .reset(reset), .clk(Clk), .Dout(rf));
  Multiplexer #(.select(4), .width(8)) multiplexer_1 (
    .in0(r0), .in1(r1), .in2(r2), .in3(r3), .in4(r4), .in5(r5), .in6(r6), .in7(r7), .in8(r8), .in9(r9),
    .in10(ra), .in11(rb), .in12(rc), .in13(rd), .in14(re), .in15(rf), .out(Port_A), .sel(RAddr_A));
  Multiplexer #(.select(4), .width(8)) multiplexer_2 (
    .in0(r0), .in1(r1), .in2(r2), .in3(r3), .in4(r4), .in5(r5), .in6(r6), .in7(r7), .in8(r8), .in9(r9),
    .in10(ra), .in11(rb), .in12(rc), .in13(rd), .in14(re), .in15(rf), .out(Port_B), .sel(RAddr_B));
endmodule

module ALU_8bit (
  input  [7:0] A,
  input  [7:0] B,
  input  [3:0] Func,
  output [7:0] ALU_OUT
);

  wire [7:0] add_sub_8bit_1_add8, and_8bit_1_and8, com_8bit_1_com8, dec_8bit_1_a_sub, inc_8bit_1_a_inc,
       lsl_8bit_1_lsl_out, lsr_8bit_1_lsr_out, or_8bit_1_or8, xor_8bit_1_xor8;

  XOR_8bit xor_8bit_1 (.A(A), .B(B), .XOR8(xor_8bit_1_xor8));
  AND_8bit and_8bit_1 (.A(A), .B(B), .AND8(and_8bit_1_and8));
  OR_8bit or_8bit_1 (.A(A), .B(B), .OR8(or_8bit_1_or8));
  ADD_SUB_8bit add_sub_8bit_1 (.A(A), .Sub(Func[2]), .B(B), .ADD8(add_sub_8bit_1_add8));
  LSR_8bit lsr_8bit_1 (.A(A), .LSR_out(lsr_8bit_1_lsr_out));
  LSL_8bit lsl_8bit_1 (.A(A), .LSL_out(lsl_8bit_1_lsl_out));
  COM_8bit com_8bit_1 (.A(A), .COM8(com_8bit_1_com8));
  INC_8bit inc_8bit_1 (.A(A), .A_inc(inc_8bit_1_a_inc));
  DEC_8bit dec_8bit_1 (.A(A), .A_sub(dec_8bit_1_a_sub));
  Multiplexer #(.select(4), .width(8)) multiplexer_1 (
    .in0(xor_8bit_1_xor8), .in1(and_8bit_1_and8), .in2(or_8bit_1_or8), .in3(add_sub_8bit_1_add8),
    .in4(lsr_8bit_1_lsr_out), .in5(lsl_8bit_1_lsl_out), .in6(com_8bit_1_com8), .in7(add_sub_8bit_1_add8),
    .in8(inc_8bit_1_a_inc), .in9(dec_8bit_1_a_sub), .out(ALU_OUT), .sel(Func));  // open: in10, in11, in12, in13, in14, in15
endmodule

module FullAdder (
  input  A,
  input  B,
  input  Cin,
  output S,
  output Cout
);

  wire and_1_out, and_2_out, and_3_out;

  and and_1 (and_1_out, A, B);
  and and_2 (and_2_out, B, Cin);
  and and_3 (and_3_out, A, Cin);
  or or_1 (Cout, and_1_out, and_2_out, and_3_out);
  xor xor_1 (S, A, B, Cin);
endmodule

module XOR_4bit (
  input  [3:0] A,
  input  [3:0] B,
  output [3:0] XOR4
);

  assign XOR4 = A ^ B;  // XOR_Gate xor_1, 4 bits wide
endmodule

module XOR_8bit (
  input  [7:0] A,
  input  [7:0] B,
  output [7:0] XOR8
);

  XOR_4bit xor_4bit_1 (.A(A[3:0]), .B(B[3:0]), .XOR4(XOR8[3:0]));
  XOR_4bit xor_4bit_2 (.A(A[7:4]), .B(B[7:4]), .XOR4(XOR8[7:4]));
endmodule

module AND_4bit (
  input  [3:0] A,
  input  [3:0] B,
  output [3:0] AND4
);

  assign AND4 = A & B;  // AND_Gate and_1, 4 bits wide
endmodule

module AND_8bit (
  input  [7:0] A,
  input  [7:0] B,
  output [7:0] AND8
);

  AND_4bit and_4bit_1 (.A(A[3:0]), .B(B[3:0]), .AND4(AND8[3:0]));
  AND_4bit and_4bit_2 (.A(A[7:4]), .B(B[7:4]), .AND4(AND8[7:4]));
endmodule

module OR_4bit (
  input  [3:0] A,
  input  [3:0] B,
  output [3:0] OR4
);

  assign OR4 = A | B;  // OR_Gate or_1, 4 bits wide
endmodule

module OR_8bit (
  input  [7:0] A,
  input  [7:0] B,
  output [7:0] OR8
);

  OR_4bit or_4bit_1 (.A(A[3:0]), .B(B[3:0]), .OR4(OR8[3:0]));
  OR_4bit or_4bit_2 (.A(A[7:4]), .B(B[7:4]), .OR4(OR8[7:4]));
endmodule

module ADD_SUB_4bit (
  input  [3:0] A,
  input  Sub,
  input  [3:0] B,
  output Carry,
  output [3:0] ADD4
);

  wire fulladder_2_cout, fulladder_3_cout, fulladder_4_cout;
  wire [3:0] com_4bit_1_com4, multiplexer_1_out;

  COM_4bit com_4bit_1 (.A(B), .COM4(com_4bit_1_com4));
  Multiplexer #(.width(4)) multiplexer_1 (.in0(B), .in1(com_4bit_1_com4), .out(multiplexer_1_out), .sel(Sub));
  FullAdder fulladder_1 (.A(A[3]), .B(multiplexer_1_out[3]), .Cin(fulladder_2_cout), .S(ADD4[3]), .Cout(Carry));
  FullAdder fulladder_2 (
    .A(A[2]), .B(multiplexer_1_out[2]), .Cin(fulladder_3_cout), .S(ADD4[2]), .Cout(fulladder_2_cout));
  FullAdder fulladder_3 (
    .A(A[1]), .B(multiplexer_1_out[1]), .Cin(fulladder_4_cout), .S(ADD4[1]), .Cout(fulladder_3_cout));
  FullAdder fulladder_4 (.A(A[0]), .B(multiplexer_1_out[0]), .Cin(Sub), .S(ADD4[0]), .Cout(fulladder_4_cout));
endmodule

module ADD_SUB_8bit (
  input  [7:0] A,
  input  Sub,
  input  [7:0] B,
  output [7:0] ADD8
);

  wire fulladder_2_cout, fulladder_3_cout, fulladder_4_cout, fulladder_5_cout, fulladder_6_cout,
       fulladder_7_cout, fulladder_8_cout;
  wire [7:0] com_8bit_1_com8, multiplexer_1_out;

  COM_8bit com_8bit_1 (.A(B), .COM8(com_8bit_1_com8));
  Multiplexer #(.width(8)) multiplexer_1 (.in0(B), .in1(com_8bit_1_com8), .out(multiplexer_1_out), .sel(Sub));
  FullAdder fulladder_1 (.A(A[7]), .B(multiplexer_1_out[7]), .Cin(fulladder_2_cout), .S(ADD8[7]));  // open: Cout
  FullAdder fulladder_2 (
    .A(A[6]), .B(multiplexer_1_out[6]), .Cin(fulladder_3_cout), .S(ADD8[6]), .Cout(fulladder_2_cout));
  FullAdder fulladder_3 (
    .A(A[5]), .B(multiplexer_1_out[5]), .Cin(fulladder_4_cout), .S(ADD8[5]), .Cout(fulladder_3_cout));
  FullAdder fulladder_4 (
    .A(A[4]), .B(multiplexer_1_out[4]), .Cin(fulladder_5_cout), .S(ADD8[4]), .Cout(fulladder_4_cout));
  FullAdder fulladder_5 (
    .A(A[3]), .B(multiplexer_1_out[3]), .Cin(fulladder_6_cout), .S(ADD8[3]), .Cout(fulladder_5_cout));
  FullAdder fulladder_6 (
    .A(A[2]), .B(multiplexer_1_out[2]), .Cin(fulladder_7_cout), .S(ADD8[2]), .Cout(fulladder_6_cout));
  FullAdder fulladder_7 (
    .A(A[1]), .B(multiplexer_1_out[1]), .Cin(fulladder_8_cout), .S(ADD8[1]), .Cout(fulladder_7_cout));
  FullAdder fulladder_8 (.A(A[0]), .B(multiplexer_1_out[0]), .Cin(Sub), .S(ADD8[0]), .Cout(fulladder_8_cout));
endmodule

module LSR_4bit (
  input  [3:0] A,
  output [3:0] LSR_out
);


  assign LSR_out = {1'b0, A[3:1]};
endmodule

module LSR_8bit (
  input  [7:0] A,
  output [7:0] LSR_out
);


  assign LSR_out = {1'b0, A[7:1]};
endmodule

module LSL_4bit (
  input  [3:0] A,
  output [3:0] LSL_out
);


  assign LSL_out = {A[2:0], 1'b0};
endmodule

module LSL_8bit (
  input  [7:0] A,
  output [7:0] LSL_out
);


  assign LSL_out = {A[6:0], 1'b0};
endmodule

module COM_4bit (
  input  [3:0] A,
  output [3:0] COM4
);

  assign COM4 = ~A;  // NOT_Gate not_1, 4 bits wide
endmodule

module COM_8bit (
  input  [7:0] A,
  output [7:0] COM8
);

  COM_4bit com_4bit_1 (.A(A[3:0]), .COM4(COM8[3:0]));
  COM_4bit com_4bit_2 (.A(A[7:4]), .COM4(COM8[7:4]));
endmodule

module INC_8bit (
  input  [7:0] A,
  output [7:0] A_inc
);

  wire not_1_out, not_2_out, not_3_out, not_4_out, not_5_out, not_6_out, not_7_out, or_1_out, or_2_out,
       or_3_out, or_4_out, or_5_out, or_6_out, or_7_out, or_8_out, or_9_out, or_10_out, or_11_out, or_12_out,
       or_13_out, or_14_out, or_15_out, or_16_out, or_17_out, or_18_out, or_19_out, or_20_out, or_21_out,
       or_22_out, or_23_out, or_24_out, or_25_out, or_26_out, or_27_out, or_28_out, or_29_out, or_30_out,
       or_31_out, or_32_out, or_33_out, or_34_out, or_35_out;

  not not_1 (not_1_out, A[7]);
  not not_2 (not_2_out, A[6]);
  not not_3 (not_3_out, A[5]);
  not not_4 (not_4_out, A[4]);
  not not_5 (not_5_out, A[3]);
  not not_6 (not_6_out, A[2]);
  not not_7 (not_7_out, A[1]);
  not not_8 (A_inc[0], A[0]);
  or or_1 (or_1_out, A[7], A[6]);
  or or_2 (or_2_out, A[7], A[5]);
  or or_3 (or_3_out, A[7], A[4]);
  or or_4 (or_4_out, A[7], A[3]);
  or or_5 (or_5_out, A[7], A[2]);
  or or_6 (or_6_out, A[7], A[1]);
  or or_7 (or_7_out, A[7], A[0]);
  or or_8 (or_8_out, not_1_out, not_2_out, not_3_out, not_4_out, not_5_out, not_6_out, not_7_out, A_inc[0]);
  or or_9 (or_9_out, A[6], A[5]);
  or or_10 (or_10_out, A[6], A[4]);
  or or_11 (or_11_out, A[6], A[3]);
  or or_12 (or_12_out, A[6], A[2]);
  or or_13 (or_13_out, A[6], A[1]);
  or or_14 (or_14_out, A[6], A[0]);
  or or_15 (or_15_out, not_2_out, not_3_out, not_4_out, not_5_out, not_6_out, not_7_out, A_inc[0]);
  or or_16 (or_16_out, A[5], A[4]);
  or or_17 (or_17_out, A[5], A[3]);
  or or_18 (or_18_out, A[5], A[2]);
  or or_19 (or_19_out, A[5], A[1]);
  or or_20 (or_20_out, A[5], A[0]);
  or or_21 (or_21_out, not_3_out, not_4_out, not_5_out, not_6_out, not_7_out, A_inc[0]);
  or or_22 (or_22_out, A[4], A[3]);
  or or_23 (or_23_out, A[4], A[2]);
  or or_24 (or_24_out, A[4], A[1]);
  or or_25 (or_25_out, A[4], A[0]);
  or or_26 (or_26_out, not_4_out, not_5_out, not_6_out, not_7_out, A_inc[0]);
  or or_27 (or_27_out, A[3], A[2]);
  or or_28 (or_28_out, A[3], A[1]);
  or or_29 (or_29_out, A[3], A[0]);
  or or_30 (or_30_out, not_5_out, not_6_out, not_7_out, A_inc[0]);
  or or_31 (or_31_out, A[2], A[1]);
  or or_32 (or_32_out, A[2], A[0]);
  or or_33 (or_33_out, not_6_out, not_7_out, A_inc[0]);
  or or_34 (or_34_out, A[1], A[0]);
  or or_35 (or_35_out, not_7_out, A_inc[0]);
  and and_1 (A_inc[7], or_1_out, or_2_out, or_3_out, or_4_out, or_5_out, or_6_out, or_7_out, or_8_out);
  and and_2 (A_inc[6], or_9_out, or_10_out, or_11_out, or_12_out, or_13_out, or_14_out, or_15_out);
  and and_3 (A_inc[5], or_16_out, or_17_out, or_18_out, or_19_out, or_20_out, or_21_out);
  and and_4 (A_inc[4], or_22_out, or_23_out, or_24_out, or_25_out, or_26_out);
  and and_5 (A_inc[3], or_27_out, or_28_out, or_29_out, or_30_out);
  and and_6 (A_inc[2], or_31_out, or_32_out, or_33_out);
  and and_7 (A_inc[1], or_34_out, or_35_out);

  // Notes on the sheet:
  //   This Circuit was automatically generated by Logisim!
endmodule

module DEC_8bit (
  input  [7:0] A,
  output [7:0] A_sub
);

  wire not_1_out, not_2_out, not_3_out, not_4_out, not_5_out, not_6_out, not_7_out, or_1_out, or_2_out,
       or_3_out, or_4_out, or_5_out, or_6_out, or_7_out, or_8_out, or_9_out, or_10_out, or_11_out, or_12_out,
       or_13_out, or_14_out, or_15_out, or_16_out, or_17_out, or_18_out, or_19_out, or_20_out, or_21_out,
       or_22_out, or_23_out, or_24_out, or_25_out, or_26_out, or_27_out, or_28_out, or_29_out, or_30_out,
       or_31_out, or_32_out, or_33_out, or_34_out, or_35_out;

  not not_1 (not_1_out, A[7]);
  not not_2 (not_2_out, A[6]);
  not not_3 (not_3_out, A[5]);
  not not_4 (not_4_out, A[4]);
  not not_5 (not_5_out, A[3]);
  not not_6 (not_6_out, A[2]);
  not not_7 (not_7_out, A[1]);
  not not_8 (A_sub[0], A[0]);
  or or_1 (or_1_out, A[7], A_sub[0]);
  or or_2 (or_2_out, A[7], not_7_out);
  or or_3 (or_3_out, A[7], not_6_out);
  or or_4 (or_4_out, A[7], not_5_out);
  or or_5 (or_5_out, A[7], not_4_out);
  or or_6 (or_6_out, A[7], not_3_out);
  or or_7 (or_7_out, A[7], not_2_out);
  or or_8 (or_8_out, not_1_out, A[6], A[5], A[4], A[3], A[2], A[1], A[0]);
  or or_9 (or_9_out, A[6], A_sub[0]);
  or or_10 (or_10_out, A[6], not_7_out);
  or or_11 (or_11_out, A[6], not_6_out);
  or or_12 (or_12_out, A[6], not_5_out);
  or or_13 (or_13_out, A[6], not_4_out);
  or or_14 (or_14_out, A[6], not_3_out);
  or or_15 (or_15_out, not_2_out, A[5], A[4], A[3], A[2], A[1], A[0]);
  or or_16 (or_16_out, A[5], A_sub[0]);
  or or_17 (or_17_out, A[5], not_7_out);
  or or_18 (or_18_out, A[5], not_6_out);
  or or_19 (or_19_out, A[5], not_5_out);
  or or_20 (or_20_out, A[5], not_4_out);
  or or_21 (or_21_out, not_3_out, A[4], A[3], A[2], A[1], A[0]);
  or or_22 (or_22_out, A[4], A_sub[0]);
  or or_23 (or_23_out, A[4], not_7_out);
  or or_24 (or_24_out, A[4], not_6_out);
  or or_25 (or_25_out, A[4], not_5_out);
  or or_26 (or_26_out, not_4_out, A[3], A[2], A[1], A[0]);
  or or_27 (or_27_out, A[3], A_sub[0]);
  or or_28 (or_28_out, A[3], not_7_out);
  or or_29 (or_29_out, A[3], not_6_out);
  or or_30 (or_30_out, not_5_out, A[2], A[1], A[0]);
  or or_31 (or_31_out, A[2], A_sub[0]);
  or or_32 (or_32_out, A[2], not_7_out);
  or or_33 (or_33_out, not_6_out, A[1], A[0]);
  or or_34 (or_34_out, A[1], A_sub[0]);
  or or_35 (or_35_out, not_7_out, A[0]);
  and and_1 (A_sub[7], or_1_out, or_2_out, or_3_out, or_4_out, or_5_out, or_6_out, or_7_out, or_8_out);
  and and_2 (A_sub[6], or_9_out, or_10_out, or_11_out, or_12_out, or_13_out, or_14_out, or_15_out);
  and and_3 (A_sub[5], or_16_out, or_17_out, or_18_out, or_19_out, or_20_out, or_21_out);
  and and_4 (A_sub[4], or_22_out, or_23_out, or_24_out, or_25_out, or_26_out);
  and and_5 (A_sub[3], or_27_out, or_28_out, or_29_out, or_30_out);
  and and_6 (A_sub[2], or_31_out, or_32_out, or_33_out);
  and and_7 (A_sub[1], or_34_out, or_35_out);

  // Notes on the sheet:
  //   This Circuit was automatically generated by Logisim!
endmodule

module Compare_2bit (
  input  [1:0] A,
  input  [1:0] B,
  output Same
);

  wire and_1_out, and_2_out, not_1_out, not_2_out, not_3_out, not_4_out, or_1_out, or_2_out, or_3_out,
       or_4_out;

  not not_1 (not_1_out, A[1]);
  not not_2 (not_2_out, A[0]);
  not not_3 (not_3_out, B[1]);
  not not_4 (not_4_out, B[0]);
  or or_1 (or_1_out, A[0], not_4_out);
  or or_2 (or_2_out, A[1], not_3_out);
  or or_3 (or_3_out, not_2_out, B[0]);
  or or_4 (or_4_out, not_1_out, B[1]);
  and and_1 (and_1_out, or_1_out, or_2_out);
  and and_2 (and_2_out, or_3_out, or_4_out);
  and and_3 (Same, and_1_out, and_2_out);
endmodule

module Compare_8bit (
  input  [7:0] A,
  input  [7:0] B,
  output Same
);

  wire and_1_out, and_2_out, compare_2bit_1_same, compare_2bit_2_same, compare_2bit_3_same,
       compare_2bit_4_same;

  Compare_2bit compare_2bit_1 (.A(A[1:0]), .B(B[1:0]), .Same(compare_2bit_1_same));
  Compare_2bit compare_2bit_2 (.A(A[3:2]), .B(B[3:2]), .Same(compare_2bit_2_same));
  Compare_2bit compare_2bit_3 (.A(A[5:4]), .B(B[5:4]), .Same(compare_2bit_3_same));
  Compare_2bit compare_2bit_4 (.A(A[7:6]), .B(B[7:6]), .Same(compare_2bit_4_same));
  and and_1 (and_1_out, compare_2bit_1_same, compare_2bit_2_same);
  and and_2 (and_2_out, compare_2bit_3_same, compare_2bit_4_same);
  and and_3 (Same, and_1_out, and_2_out);
endmodule

module Jump_EN_Logic (
  input  is_jump,
  input  [1:0] jump_type,
  input  c,
  output load_enable
);

  wire and_1_out, and_2_out, and_3_out, and_4_out, and_5_out, not_1_out, not_2_out, not_3_out, or_1_out;

  not not_1 (not_1_out, jump_type[1]);
  not not_2 (not_2_out, jump_type[0]);
  not not_3 (not_3_out, c);
  and and_1 (and_1_out, is_jump, not_2_out);
  and and_2 (and_2_out, is_jump, not_1_out);
  and and_3 (and_3_out, and_1_out, c);
  and and_4 (and_4_out, is_jump, jump_type[0]);
  or or_1 (or_1_out, and_2_out, and_3_out);
  and and_5 (and_5_out, and_4_out, not_3_out);
  or or_2 (load_enable, or_1_out, and_5_out);
endmodule

module Write_100s (
  input  [3:0] bcd_100s,
  output used
);

  wire or_1_out, or_2_out;

  or or_1 (or_1_out, bcd_100s[0], bcd_100s[1]);
  or or_2 (or_2_out, bcd_100s[2], bcd_100s[3]);
  or or_3 (used, or_1_out, or_2_out);
endmodule

module Write_10s (
  input  [3:0] bcd_10s,
  input  used_100s,
  output used
);

  wire or_1_out, or_2_out, or_3_out;

  or or_1 (or_1_out, used_100s, bcd_10s[0]);
  or or_2 (or_2_out, or_1_out, bcd_10s[1]);
  or or_3 (or_3_out, bcd_10s[2], bcd_10s[3]);
  or or_4 (used, or_2_out, or_3_out);
endmodule

module Number_to_ASCII (
  input  [3:0] bcd,
  output [6:0] ascii_num
);


  assign ascii_num = {3'b011, bcd};
endmodule

module ASCII_Digits (
  input  [6:0] num,
  output [6:0] ASCII_100s,
  output Use_100s,
  output [6:0] ASCII_10s,
  output Use_10s,
  output [6:0] ASCII_1s
);

  wire [3:0] binary_to_bcd_converter_1_p2, binary_to_bcd_converter_1_p3, binary_to_bcd_converter_1_p4;

  // Binary_to_BCD_converter #(.binvalue(7)) binary_to_bcd_converter_1: pin names not known; wires that end beside it: num, binary_to_bcd_converter_1_p2, binary_to_bcd_converter_1_p3, binary_to_bcd_converter_1_p4
  Number_to_ASCII number_to_ascii_1 (.bcd(binary_to_bcd_converter_1_p2), .ascii_num(ASCII_100s));
  Write_100s write_100s_1 (.bcd_100s(binary_to_bcd_converter_1_p2), .used(Use_100s));
  Number_to_ASCII number_to_ascii_2 (.bcd(binary_to_bcd_converter_1_p3), .ascii_num(ASCII_10s));
  Write_10s write_10s_1 (.bcd_10s(binary_to_bcd_converter_1_p3), .used_100s(Use_100s), .used(Use_10s));
  Number_to_ASCII number_to_ascii_3 (.bcd(binary_to_bcd_converter_1_p4), .ascii_num(ASCII_1s));
endmodule

module Queue_shift (
  input  [7:0] r0_out,
  input  [7:0] r1_out,
  input  [7:0] r2_out,
  input  [7:0] r3_out,
  input  [7:0] Data_in,
  input  shift_enable,
  output [7:0] dequeue,
  output [7:0] r0_in,
  output [7:0] r1_in,
  output [7:0] r2_in,
  output [7:0] r3_in
);

  wire [7:0] multiplexer_1_out, multiplexer_2_out, multiplexer_3_out, multiplexer_4_out, multiplexer_5_out,
       multiplexer_6_out, multiplexer_7_out, multiplexer_8_out, multiplexer_9_out, multiplexer_10_out,
       multiplexer_11_out, multiplexer_12_out, multiplexer_13_out, multiplexer_14_out;

  Multiplexer #(.width(8)) multiplexer_1 (.in0(Data_in), .in1(r3_out), .out(multiplexer_1_out), .sel(r3_out[7]));
  Multiplexer #(.width(8)) multiplexer_2 (
    .in0(multiplexer_1_out), .in1(r2_out), .out(multiplexer_2_out), .sel(r2_out[7]));
  Multiplexer #(.width(8)) multiplexer_3 (.in0({8{1'b0}}), .in1(Data_in), .out(multiplexer_3_out), .sel(r3_out[7]));
  Multiplexer #(.width(8)) multiplexer_4 (
    .in0(multiplexer_3_out), .in1(multiplexer_1_out), .out(multiplexer_4_out), .sel(r2_out[7]));
  Multiplexer #(.width(8)) multiplexer_5 (
    .in0(multiplexer_2_out), .in1(r1_out), .out(multiplexer_5_out), .sel(r1_out[7]));
  Multiplexer #(.width(8)) multiplexer_6 (
    .in0({8{1'b0}}), .in1(multiplexer_3_out), .out(multiplexer_6_out), .sel(r2_out[7]));
  Multiplexer #(.width(8)) multiplexer_7 (
    .in0(multiplexer_4_out), .in1(multiplexer_2_out), .out(multiplexer_7_out), .sel(r1_out[7]));
  Multiplexer #(.width(8)) multiplexer_8 (
    .in0(multiplexer_6_out), .in1(multiplexer_4_out), .out(multiplexer_8_out), .sel(r1_out[7]));
  Multiplexer #(.width(8)) multiplexer_9 (
    .in0({8{1'b0}}), .in1(multiplexer_6_out), .out(multiplexer_9_out), .sel(r1_out[7]));
  Multiplexer #(.width(8)) multiplexer_10 (
    .in0(multiplexer_5_out), .in1(r0_out), .out(multiplexer_10_out), .sel(r0_out[7]));
  Multiplexer #(.width(8)) multiplexer_11 (
    .in0(multiplexer_7_out), .in1(multiplexer_5_out), .out(multiplexer_11_out), .sel(r0_out[7]));
  Multiplexer #(.width(8)) multiplexer_12 (
    .in0(multiplexer_8_out), .in1(multiplexer_7_out), .out(multiplexer_12_out), .sel(r0_out[7]));
  Multiplexer #(.width(8)) multiplexer_13 (
    .in0(multiplexer_9_out), .in1(multiplexer_8_out), .out(multiplexer_13_out), .sel(r0_out[7]));
  Multiplexer #(.width(8)) multiplexer_14 (
    .in0({8{1'b0}}), .in1(multiplexer_9_out), .out(multiplexer_14_out), .sel(r0_out[7]));
  Multiplexer #(.width(8)) multiplexer_15 (.in0(r0_out), .in1(multiplexer_10_out), .out(dequeue), .sel(shift_enable));
  Multiplexer #(.width(8)) multiplexer_16 (.in0(r0_out), .in1(multiplexer_11_out), .out(r0_in), .sel(shift_enable));
  Multiplexer #(.width(8)) multiplexer_17 (.in0(r1_out), .in1(multiplexer_12_out), .out(r1_in), .sel(shift_enable));
  Multiplexer #(.width(8)) multiplexer_18 (.in0(r2_out), .in1(multiplexer_13_out), .out(r2_in), .sel(shift_enable));
  Multiplexer #(.width(8)) multiplexer_19 (.in0(r3_out), .in1(multiplexer_14_out), .out(r3_in), .sel(shift_enable));
endmodule

module Regs_in_use (
  input  [7:0] r0,
  input  [7:0] r1,
  input  [7:0] r2,
  input  [7:0] r3,
  output [3:0] used_regs
);


  assign used_regs = {r3[7], r2[7], r1[7], r0[7]};
endmodule

module Reg_prevent_race (
  input  Use_100s,
  input  Use_10s,
  input  [3:0] regs_in_use,
  output wait_shift
);

  wire and_1_out, and_2_out, and_3_out, or_1_out, or_2_out;

  and and_1 (and_1_out, Use_10s, regs_in_use[2]);
  and and_2 (and_2_out, Use_100s, regs_in_use[1]);
  and and_3 (and_3_out, Use_100s, regs_in_use[2]);
  or or_1 (or_1_out, regs_in_use[3], and_1_out);
  or or_2 (or_2_out, and_2_out, and_3_out);
  or or_3 (wait_shift, or_1_out, or_2_out);
endmodule

module parallel_ld_select (
  input  Use_100s,
  input  Use_10s,
  input  [3:0] regs_in_use,
  output [1:0] reg_100s,
  output [1:0] reg_10s,
  output [1:0] reg_1s,
  output interrupt_bar
);

  wire and_1_out, and_2_out, and_3_out, and_4_out, and_5_out, and_6_out, and_7_out, and_8_out, and_9_out,
       and_10_out, and_11_out, and_12_out, and_13_out, and_14_out, and_15_out, and_16_out, and_17_out,
       and_18_out, not_1_out, not_2_out, not_3_out, not_4_out, not_5_out, not_6_out, or_2_out, or_3_out,
       or_6_out, or_7_out, or_8_out, or_9_out;

  not not_1 (not_1_out, Use_100s);
  not not_2 (not_2_out, Use_10s);
  not not_3 (not_3_out, regs_in_use[3]);
  not not_4 (not_4_out, regs_in_use[2]);
  not not_5 (not_5_out, regs_in_use[1]);
  not not_6 (not_6_out, regs_in_use[0]);
  and and_1 (and_1_out, Use_100s, regs_in_use[0]);
  and and_2 (and_2_out, not_1_out, not_5_out);
  and and_3 (and_3_out, Use_10s, regs_in_use[0]);
  and and_4 (and_4_out, not_1_out, Use_10s);
  and and_5 (and_5_out, not_2_out, not_5_out);
  and and_6 (and_6_out, not_1_out, not_2_out);
  and and_7 (and_7_out, not_1_out, not_3_out);
  or or_1 (reg_10s[1], and_1_out, regs_in_use[1]);
  and and_8 (and_8_out, Use_100s, not_6_out);
  and and_9 (and_9_out, and_2_out, regs_in_use[0]);
  or or_2 (or_2_out, Use_100s, and_3_out);
  or or_3 (or_3_out, regs_in_use[1], regs_in_use[2]);
  and and_10 (and_10_out, and_4_out, not_6_out);
  and and_11 (and_11_out, and_5_out, regs_in_use[0]);
  and and_12 (and_12_out, and_6_out, not_3_out);
  and and_13 (and_13_out, and_7_out, not_4_out);
  and and_14 (and_14_out, Use_10s, not_3_out);
  and and_15 (and_15_out, not_4_out, not_5_out);
  or or_4 (reg_10s[0], and_8_out, and_9_out);
  or or_5 (reg_1s[1], or_2_out, or_3_out);
  or or_6 (or_6_out, and_10_out, and_11_out);
  and and_16 (and_16_out, Use_100s, regs_in_use[0]);
  and and_17 (and_17_out, Use_10s, regs_in_use[1]);
  or or_7 (or_7_out, and_12_out, and_13_out);
  and and_18 (and_18_out, and_14_out, and_15_out);
  or or_8 (or_8_out, or_6_out, and_16_out);
  or or_9 (or_9_out, and_17_out, regs_in_use[2]);
  or or_10 (interrupt_bar, or_7_out, and_18_out);
  or or_11 (reg_1s[0], or_8_out, or_9_out);

  assign reg_100s = {1'b0, regs_in_use[0]};
endmodule

module Number_Write_Logic (
  input  [6:0] num,
  input  [7:0] r0_out,
  input  [7:0] r1_out,
  input  [7:0] r2_out,
  input  [7:0] r3_out,
  input  write_num,
  output [7:0] r0_in,
  output [7:0] r1_in,
  output [7:0] r2_in,
  output [7:0] r3_in,
  output intr_bar
);

  wire and_1_out, and_2_out;
  wire [1:0] parallel_ld_select_1_reg_1s, parallel_ld_select_1_reg_10s, parallel_ld_select_1_reg_100s;
  wire [3:0] regs_in_use_1_used_regs;
  wire [6:0] ascii_digits_1_ascii_1s;
  wire [7:0] ascii_digits_1_ascii_10s, ascii_digits_1_ascii_100s;

  ASCII_Digits ascii_digits_1 (
    .num(num), .ASCII_100s(ascii_digits_1_ascii_100s[6:0]), .Use_100s(ascii_digits_1_ascii_100s[7]),
    .ASCII_10s(ascii_digits_1_ascii_10s[6:0]), .Use_10s(ascii_digits_1_ascii_10s[7]),
    .ASCII_1s(ascii_digits_1_ascii_1s));
  Regs_in_use regs_in_use_1 (.r0(r0_out), .r1(r1_out), .r2(r2_out), .r3(r3_out), .used_regs(regs_in_use_1_used_regs));
  Demultiplexer #(.enable("true"), .select(2), .width(8)) demultiplexer_1 (
    .in(ascii_digits_1_ascii_100s), .sel(parallel_ld_select_1_reg_100s), .en(and_1_out));  // open: out0, out1, out2, out3
  and and_1 (and_1_out, write_num, ascii_digits_1_ascii_100s[7]);
  and and_2 (and_2_out, ascii_digits_1_ascii_10s[7], write_num);
  parallel_ld_select parallel_ld_select_1 (
    .Use_100s(ascii_digits_1_ascii_100s[7]), .Use_10s(ascii_digits_1_ascii_10s[7]),
    .regs_in_use(regs_in_use_1_used_regs), .reg_100s(parallel_ld_select_1_reg_100s),
    .reg_10s(parallel_ld_select_1_reg_10s), .reg_1s(parallel_ld_select_1_reg_1s), .interrupt_bar(intr_bar));
  Demultiplexer #(.enable("true"), .select(2), .width(8)) demultiplexer_2 (
    .in(ascii_digits_1_ascii_10s), .sel(parallel_ld_select_1_reg_10s), .en(and_2_out));  // open: out0, out1, out2, out3
  Demultiplexer #(.enable("true"), .select(2), .width(8)) demultiplexer_3 (
    .in({write_num, ascii_digits_1_ascii_1s}), .sel(parallel_ld_select_1_reg_1s), .en(write_num));  // open: out0, out1, out2, out3

  // Other names for the same wires on the sheet: w_num = write_num
endmodule

module Display_queue (
  input  [6:0] data,
  input  Write_Data,
  input  [6:0] num,
  input  do_shift,
  input  write_num,
  input  reset,
  input  clk,
  output [7:0] dequeue,
  output intr_bar
);

  wire and_1_out, and_2_out;
  wire [1:0] parallel_ld_select_1_reg_1s, parallel_ld_select_1_reg_10s, parallel_ld_select_1_reg_100s;
  wire [3:0] regs_in_use_1_used_regs;
  wire [6:0] ascii_digits_1_ascii_1s, ascii_digits_1_ascii_10s, ascii_digits_1_ascii_100s;
  wire [7:0] r0_in, r0_out, r1_in, r1_out, r2_in, r2_out, r3_in, r3_out;
  wire [7:7] ascii_digits_1_use_10s, ascii_digits_1_use_100s;

  ASCII_Digits ascii_digits_1 (
    .num(num), .ASCII_100s(ascii_digits_1_ascii_100s), .Use_100s(ascii_digits_1_use_100s[7]),
    .ASCII_10s(ascii_digits_1_ascii_10s), .Use_10s(ascii_digits_1_use_10s[7]),
    .ASCII_1s(ascii_digits_1_ascii_1s));
  Regs_in_use regs_in_use_1 (.r0(r0_out), .r1(r1_out), .r2(r2_out), .r3(r3_out), .used_regs(regs_in_use_1_used_regs));
  and and_1 (and_1_out, write_num, ascii_digits_1_use_100s[7]);
  and and_2 (and_2_out, ascii_digits_1_use_10s[7], write_num);
  parallel_ld_select parallel_ld_select_1 (
    .Use_100s(ascii_digits_1_use_100s[7]), .Use_10s(ascii_digits_1_use_10s[7]),
    .regs_in_use(regs_in_use_1_used_regs), .reg_100s(parallel_ld_select_1_reg_100s),
    .reg_10s(parallel_ld_select_1_reg_10s), .reg_1s(parallel_ld_select_1_reg_1s), .interrupt_bar(intr_bar));
  Demultiplexer #(.enable("true"), .select(2), .width(8)) demultiplexer_1 (
    .in({ascii_digits_1_use_100s[7], ascii_digits_1_ascii_100s}), .sel(parallel_ld_select_1_reg_100s),
    .en(and_1_out));  // open: out0, out1, out2, out3
  Demultiplexer #(.enable("true"), .select(2), .width(8)) demultiplexer_2 (
    .in({ascii_digits_1_use_10s[7], ascii_digits_1_ascii_10s}), .sel(parallel_ld_select_1_reg_10s),
    .en(and_2_out));  // open: out0, out1, out2, out3
  Demultiplexer #(.enable("true"), .select(2), .width(8)) demultiplexer_3 (
    .in({write_num, ascii_digits_1_ascii_1s}), .sel(parallel_ld_select_1_reg_1s), .en(write_num));  // open: out0, out1, out2, out3
  Register_8bit register_8bit_1 (.Din(r0_in), .Write_EN(1'b1), .reset(reset), .clk(clk), .Dout(r0_out));
  Register_8bit register_8bit_2 (.Din(r1_in), .Write_EN(1'b1), .reset(reset), .clk(clk), .Dout(r1_out));
  Register_8bit register_8bit_3 (.Din(r2_in), .Write_EN(1'b1), .reset(reset), .clk(clk), .Dout(r2_out));
  Register_8bit register_8bit_4 (.Din(r3_in), .Write_EN(1'b1), .reset(reset), .clk(clk), .Dout(r3_out));
  Queue_shift queue_shift_1 (
    .r0_out(r0_out), .r1_out(r1_out), .r2_out(r2_out), .r3_out(r3_out), .Data_in({Write_Data, data}),
    .shift_enable(do_shift), .dequeue(dequeue), .r0_in(r0_in), .r1_in(r1_in), .r2_in(r2_in), .r3_in(r3_in));

  // Other names for the same wires on the sheet: w_num = write_num
endmodule
